// Logisim project Abdelmunem_Mona Logic.circ as structural Verilog: 7 circuits, main circuit main
module main (
  input  X0,
  input  Y0,
  input  Y6,
  input  _1,
  input  Y4,
  input  _1_2,
  input  Y5,
  input  Y3,
  input  Y2,
  input  Y1,
  input  X1,
  input  X2,
  input  X3,
  input  X4,
  input  _1_3,
  output P0,
  output P1,
  output P2,
  output P3,
  output P4,
  output P11,
  output P10,
  output P9,
  output P8,
  output P7,
  output P6,
  output P5
);

  wire and_1_out, and_2_out, and_3_out, and_4_out, fa_2_carry, fa_3_carry, fa_4_carry, fa_5_carry,
       fa_6_carry, fa_and_1_c_o, fa_and_1_s_o, fa_and_2_c_o, fa_and_2_s_o, fa_and_3_c_o, fa_and_3_s_o,
       fa_and_4_c_o, fa_and_4_s_o, fa_and_5_c_o, fa_and_5_s_o, fa_and_6_c_o, fa_and_6_s_o, fa_and_7_c_o,
       fa_and_7_s_o, fa_and_8_c_o, fa_and_8_s_o, fa_and_9_c_o, fa_and_9_s_o, fa_and_10_c_o, fa_and_10_s_o,
       fa_and_11_c_o, fa_and_11_s_o, fa_and_12_c_o, fa_and_13_c_o, fa_nand_1_c_o, fa_nand_1_s_o,
       fa_nand_2_c_o, fa_nand_2_s_o, fa_nand_3_c_o, fa_nand_3_s_o, fa_nand_4_c_o, fa_nand_4_s_o,
       fa_nand_5_c_o, fa_nand_5_s_o, fa_nand_6_c_o, ha_1_carry, ha_and_1_c_o, ha_and_1_s_o, ha_and_2_c_o,
       ha_and_2_s_o, ha_and_3_c_o, ha_and_3_s_o, ha_and_4_c_o, ha_and_4_s_o, ha_and_5_c_o, ha_and_5_s_o,
       ha_and_6_c_o, ha_and_6_s_o, ha_and_7_c_o, ha_nand_1_c_o, ha_nand_1_s_o, ha_nand_2_c_o, ha_nand_2_s_o,
       ha_nand_3_c_o, ha_nand_3_s_o, ha_nand_4_c_o, ha_nand_4_s_o;

  HA_NAND ha_nand_1 (.X(X3), .Y(Y6), .S_i(ha_nand_4_c_o), .C_o(ha_nand_1_c_o), .S_o(ha_nand_1_s_o));
  HA_AND ha_and_1 (.X(X4), .Y(Y6), .S_i(ha_nand_1_c_o), .C_o(ha_and_1_c_o), .S_o(ha_and_1_s_o));
  FA fa_1 (.B(ha_and_1_c_o), .C(fa_2_carry), .SUM(P11), .A(_1_3));  // open: CARRY
  HA_NAND ha_nand_2 (.X(X0), .Y(Y6), .S_i(_1), .C_o(ha_nand_2_c_o), .S_o(ha_nand_2_s_o));
  HA_NAND ha_nand_3 (.X(X1), .Y(Y6), .S_i(ha_nand_2_c_o), .C_o(ha_nand_3_c_o), .S_o(ha_nand_3_s_o));
  HA_NAND ha_nand_4 (.X(X2), .Y(Y6), .S_i(ha_nand_3_c_o), .C_o(ha_nand_4_c_o), .S_o(ha_nand_4_s_o));
  FA_NAND fa_nand_1 (.X(X4), .Y(Y5), .S_i(fa_and_2_c_o), .C_i(ha_nand_1_s_o), .C_o(fa_nand_1_c_o), .S_o(fa_nand_1_s_o));
  FA fa_2 (.B(fa_nand_1_c_o), .C(fa_3_carry), .SUM(P10), .CARRY(fa_2_carry), .A(ha_and_1_s_o));
  FA_AND fa_and_1 (.S_o(fa_and_1_s_o), .C_o(fa_and_1_c_o), .X(Y5), .S_i(ha_and_2_c_o), .C_i(ha_nand_3_s_o), .Y(X2));
  FA_AND fa_and_2 (.S_o(fa_and_2_s_o), .C_o(fa_and_2_c_o), .X(Y5), .S_i(fa_and_1_c_o), .C_i(ha_nand_4_s_o), .Y(X3));
  and and_1 (and_1_out, X0, Y5);
  HA_AND ha_and_2 (.X(X1), .Y(Y5), .S_i(ha_nand_2_s_o), .C_o(ha_and_2_c_o), .S_o(ha_and_2_s_o));
  FA_AND fa_and_3 (.S_o(fa_and_3_s_o), .C_o(fa_and_3_c_o), .X(Y4), .S_i(fa_and_4_c_o), .C_i(fa_and_1_s_o), .Y(X3));
  FA_NAND fa_nand_2 (.X(X4), .Y(Y4), .S_i(fa_and_3_c_o), .C_i(fa_and_2_s_o), .C_o(fa_nand_2_c_o), .S_o(fa_nand_2_s_o));
  FA fa_3 (.B(fa_nand_2_c_o), .C(fa_4_carry), .SUM(P9), .CARRY(fa_3_carry), .A(fa_nand_1_s_o));
  FA_AND fa_and_4 (.S_o(fa_and_4_s_o), .C_o(fa_and_4_c_o), .X(Y4), .S_i(fa_and_5_c_o), .C_i(ha_and_2_s_o), .Y(X2));
  FA_NAND fa_nand_3 (.X(X4), .Y(Y3), .S_i(fa_and_7_c_o), .C_i(fa_and_3_s_o), .C_o(fa_nand_3_c_o), .S_o(fa_nand_3_s_o));
  FA fa_4 (.B(fa_nand_3_c_o), .C(fa_5_carry), .SUM(P8), .CARRY(fa_4_carry), .A(fa_nand_2_s_o));
  HA_AND ha_and_3 (.X(X0), .Y(Y4), .S_i(_1_2), .C_o(ha_and_3_c_o), .S_o(ha_and_3_s_o));
  FA_AND fa_and_5 (.S_o(fa_and_5_s_o), .C_o(fa_and_5_c_o), .X(Y4), .S_i(and_1_out), .C_i(ha_and_3_c_o), .Y(X1));
  FA_AND fa_and_6 (.S_o(fa_and_6_s_o), .C_o(fa_and_6_c_o), .X(Y3), .S_i(ha_and_4_c_o), .C_i(fa_and_5_s_o), .Y(X2));
  FA_AND fa_and_7 (.S_o(fa_and_7_s_o), .C_o(fa_and_7_c_o), .X(Y3), .S_i(fa_and_6_c_o), .C_i(fa_and_4_s_o), .Y(X3));
  FA fa_5 (.B(fa_nand_4_c_o), .C(fa_6_carry), .SUM(P7), .CARRY(fa_5_carry), .A(fa_nand_3_s_o));
  and and_2 (and_2_out, X0, Y3);
  HA_AND ha_and_4 (.X(X1), .Y(Y3), .S_i(ha_and_3_s_o), .C_o(ha_and_4_c_o), .S_o(ha_and_4_s_o));
  FA_AND fa_and_8 (.S_o(fa_and_8_s_o), .C_o(fa_and_8_c_o), .X(Y2), .S_i(fa_and_9_c_o), .C_i(fa_and_6_s_o), .Y(X3));
  FA_NAND fa_nand_4 (.X(X4), .Y(Y2), .S_i(fa_and_8_c_o), .C_i(fa_and_7_s_o), .C_o(fa_nand_4_c_o), .S_o(fa_nand_4_s_o));
  HA_AND ha_and_5 (.X(X1), .Y(Y2), .S_i(and_2_out), .C_o(ha_and_5_c_o), .S_o(ha_and_5_s_o));
  FA_AND fa_and_9 (.S_o(fa_and_9_s_o), .C_o(fa_and_9_c_o), .X(Y2), .S_i(ha_and_5_c_o), .C_i(ha_and_4_s_o), .Y(X2));
  FA_NAND fa_nand_5 (.X(X4), .Y(Y1), .S_i(fa_and_11_c_o), .C_i(fa_and_8_s_o), .C_o(fa_nand_5_c_o), .S_o(fa_nand_5_s_o));
  FA fa_6 (.B(fa_nand_5_c_o), .C(ha_1_carry), .SUM(P6), .CARRY(fa_6_carry), .A(fa_nand_4_s_o));
  and and_3 (and_3_out, X0, Y2);
  FA_AND fa_and_10 (.S_o(fa_and_10_s_o), .C_o(fa_and_10_c_o), .X(Y1), .S_i(ha_and_6_c_o), .C_i(ha_and_5_s_o), .Y(X2));
  FA_AND fa_and_11 (.S_o(fa_and_11_s_o), .C_o(fa_and_11_c_o), .X(Y1), .S_i(fa_and_10_c_o), .C_i(fa_and_9_s_o), .Y(X3));
  HA ha_1 (.A(fa_nand_6_c_o), .B(fa_nand_5_s_o), .SUM(P5), .CARRY(ha_1_carry));
  and and_4 (and_4_out, X0, Y1);
  HA_AND ha_and_6 (.X(X1), .Y(Y1), .S_i(and_3_out), .C_o(ha_and_6_c_o), .S_o(ha_and_6_s_o));
  FA_AND fa_and_12 (.S_o(P3), .C_o(fa_and_12_c_o), .X(Y0), .S_i(fa_and_13_c_o), .C_i(fa_and_10_s_o), .Y(X3));
  FA_NAND fa_nand_6 (.X(X4), .Y(Y0), .S_i(fa_and_12_c_o), .C_i(fa_and_11_s_o), .C_o(fa_nand_6_c_o), .S_o(P4));
  HA_AND ha_and_7 (.X(X1), .Y(Y0), .S_i(and_4_out), .C_o(ha_and_7_c_o), .S_o(P1));
  FA_AND fa_and_13 (.S_o(P2), .C_o(fa_and_13_c_o), .X(Y0), .S_i(ha_and_7_c_o), .C_i(ha_and_6_s_o), .Y(X2));
  and and_5 (P0, X0, Y0);
endmodule

module FA (
  input  A,
  input  B,
  input  C,
  output SUM,
  output CARRY
);

  wire and_1_out, and_2_out, xor_1_out;

  xor xor_1 (xor_1_out, A, B);
  and and_1 (and_1_out, A, B);
  and and_2 (and_2_out, xor_1_out, C);
  xor xor_2 (SUM, xor_1_out, C);
  or or_1 (CARRY, and_2_out, and_1_out);
endmodule

module FA_AND (
  input  X,
  input  Y,
  input  S_i,
  input  C_i,
  output C_o,
  output S_o
);

  wire and_1_out;

  and and_1 (and_1_out, X, Y);
  FA FA (.B(S_i), .C(C_i), .SUM(S_o), .CARRY(C_o), .A(and_1_out));
endmodule

module FA_NAND (
  input  X,
  input  Y,
  input  S_i,
  input  C_i,
  output C_o,
  output S_o
);

  wire nand_1_out;

  nand nand_1 (nand_1_out, X, Y);
  FA FA (.B(S_i), .C(C_i), .SUM(S_o), .CARRY(C_o), .A(nand_1_out));
endmodule

module HA (
  input  A,
  input  B,
  output SUM,
  output CARRY
);

  xor xor_1 (SUM, A, B);
  and and_1 (CARRY, A, B);
endmodule

module HA_AND (
  input  X,
  input  Y,
  input  S_i,
  output C_o,
  output S_o
);

  wire and_1_out;

  and and_1 (and_1_out, X, Y);
  HA ha_1 (.A(S_i), .B(and_1_out), .SUM(S_o), .CARRY(C_o));
endmodule

module HA_NAND (
  input  X,
  input  Y,
  input  S_i,
  output C_o,
  output S_o
);

  wire nand_1_out;

  nand nand_1 (nand_1_out, X, Y);
  HA ha_1 (.A(S_i), .B(nand_1_out), .SUM(S_o), .CARRY(C_o));
endmodule
